// Logisim project ALU.circ as structural Verilog: 30 circuits, main circuit main
module main (
  input  [31:0] _32_bit_A,
  input  [31:0] _32_bit_B,
  input  [5:0] OpCode,
  input  clk,
  output [31:0] _32_bit_C,
  output Carryout,
  output Zero,
  output Overflow
);

  wire n32_bit_adder_1_carryout, n32_bit_adder_1_overflow, n32_bit_shift_left_1_overflow,
       n32_bit_subtractor_1_carryout, n32_bit_subtractor_1_overflow, not_1_out, not_2_out, or_2_out, or_3_out;
  wire [31:0] and_out, myinst_1__32_bit_c, n16_to_32_bit_multiplier_1__32_bit_c,
       n32_bit_adder_1__32_bit_output, n32_bit_set_less_than_1__32_bit_c, n32_bit_shift_left_1__32_bit_c,
       n32_bit_shift_right_1__32_bit_c, n32_bit_shift_right_arithmatic_1__32_bit_c,
       n32_bit_subtractor_1__32_bit_output, or_out, xor_out;

  _32_bit_subtractor u_32_bit_subtractor_1 (
    ._32_bit_A(_32_bit_A), ._32_bit_B(_32_bit_B), ._32_bit_output(n32_bit_subtractor_1__32_bit_output),
    .carryout(n32_bit_subtractor_1_carryout), .overflow(n32_bit_subtractor_1_overflow));
  _32_bit_adder u_32_bit_adder_1 (
    ._32_bit_A(_32_bit_A), ._32_bit_B(_32_bit_B), ._32_bit_output(n32_bit_adder_1__32_bit_output),
    .carryout(n32_bit_adder_1_carryout), .overflow(n32_bit_adder_1_overflow));
  _16_to_32_bit_multiplier u_16_to_32_bit_multiplier_1 (
    ._16_bit_A(_32_bit_A[15:0]), ._16_bit_B(_32_bit_B[15:0]), ._32_bit_C(n16_to_32_bit_multiplier_1__32_bit_c));
  assign and_out = _32_bit_A & _32_bit_B;  // AND_Gate and, 32 bits wide
  assign or_out = _32_bit_A | _32_bit_B;  // OR_Gate or, 32 bits wide
  _32_bit_shift_left u_32_bit_shift_left_1 (
    ._32_bit_A(_32_bit_A), .B(_32_bit_B[4:0]), ._32_bit_C(n32_bit_shift_left_1__32_bit_c),
    .overflow(n32_bit_shift_left_1_overflow));
  _32_bit_set_less_than u_32_bit_set_less_than_1 (
    ._32_bit_A(_32_bit_A), ._32_bit_B(_32_bit_B), ._32_bit_C(n32_bit_set_less_than_1__32_bit_c));
  _32_bit_shift_right_arithmatic u_32_bit_shift_right_arithmatic_1 (
    ._32_bit_A(_32_bit_A), .B(_32_bit_B[4:0]), ._32_bit_C(n32_bit_shift_right_arithmatic_1__32_bit_c));
  _32_bit_shift_right u_32_bit_shift_right_1 (
    ._32_bit_A(_32_bit_A), .B(_32_bit_B[4:0]), ._32_bit_C(n32_bit_shift_right_1__32_bit_c));
  myInst myinst_1 (._3_bit_A(_32_bit_B[3:0]), .clk(clk), ._32_bit_C(myinst_1__32_bit_c));
  assign xor_out = _32_bit_A ^ _32_bit_B;  // XOR_Gate xor, 32 bits wide
  Multiplexer #(.select(2), .disabled(0)) multiplexer_1 (
    .in0(n32_bit_subtractor_1_carryout), .in1(n32_bit_adder_1_carryout), .in2(1'b0), .in3(1'b0),
    .out(Carryout), .sel(OpCode[1:0]), .en(not_1_out));
  not not_1 (not_1_out, or_2_out);
  Multiplexer #(.select(4), .width(32), .enable("false")) multiplexer_2 (
    .in0(n32_bit_subtractor_1__32_bit_output), .in1(n32_bit_adder_1__32_bit_output),
    .in2(n16_to_32_bit_multiplier_1__32_bit_c), .in3(and_out), .in4(or_out), .in5(xor_out),
    .in6(n32_bit_shift_left_1__32_bit_c), .in7(n32_bit_set_less_than_1__32_bit_c),
    .in8(n32_bit_shift_right_arithmatic_1__32_bit_c), .in9(n32_bit_shift_right_1__32_bit_c),
    .in10(n32_bit_adder_1__32_bit_output), .in11(n32_bit_adder_1__32_bit_output),
    .in12(n32_bit_subtractor_1__32_bit_output), .in13(n32_bit_subtractor_1__32_bit_output),
    .in15(myinst_1__32_bit_c), .out(_32_bit_C), .sel(OpCode[3:0]));  // open: in14
  not not_2 (not_2_out, OpCode[3]);
  Multiplexer #(.select(3), .disabled(0)) multiplexer_3 (
    .in0(n32_bit_subtractor_1_overflow), .in1(n32_bit_adder_1_overflow), .in2(1'b0), .in3(1'b0), .in4(1'b0),
    .in5(1'b0), .in6(n32_bit_shift_left_1_overflow), .in7(1'b0), .out(Overflow), .sel(OpCode[2:0]),
    .en(not_2_out));
  or or_2 (or_2_out, OpCode[2], OpCode[3]);
  or or_3 (or_3_out, _32_bit_C[0], _32_bit_C[1], _32_bit_C[2], _32_bit_C[3], _32_bit_C[4], _32_bit_C[5], _32_bit_C[6], _32_bit_C[7], _32_bit_C[8], _32_bit_C[9], _32_bit_C[10], _32_bit_C[11], _32_bit_C[12], _32_bit_C[13], _32_bit_C[14], _32_bit_C[15], _32_bit_C[17], _32_bit_C[18], _32_bit_C[19], _32_bit_C[20], _32_bit_C[21], _32_bit_C[22], _32_bit_C[23], _32_bit_C[24], _32_bit_C[25], _32_bit_C[26], _32_bit_C[27], _32_bit_C[28], _32_bit_C[29], _32_bit_C[30], _32_bit_C[31], _32_bit_C[16]);
  not not_3 (Zero, or_3_out);
endmodule

// FA
module _1_bit_adder (
  input  A,
  input  B,
  input  Carry,
  output Sum,
  output Carry_Out
);

  wire and_1_out, and_2_out, xor_1_out;

  xor xor_1 (xor_1_out, A, B);
  xor xor_2 (Sum, xor_1_out, Carry);
  and and_1 (and_1_out, Carry, xor_1_out);
  and and_2 (and_2_out, A, B);
  or or_1 (Carry_Out, and_1_out, and_2_out);

  // Other names for the same wires on the sheet: C = Carry
endmodule

// HA
module _1_bit_half_adder (
  input  _1_bit_A,
  input  _1_bit_B,
  output Sum,
  output Carry
);

  xor xor_1 (Sum, _1_bit_A, _1_bit_B);
  and and_1 (Carry, _1_bit_A, _1_bit_B);
endmodule

// add
module _32_bit_adder (
  input  [31:0] _32_bit_A,
  input  [31:0] _32_bit_B,
  output [31:0] _32_bit_output,
  output carryout,
  output overflow
);

  wire n1_bit_adder_1_carry_out, n1_bit_adder_2_carry_out, n1_bit_adder_3_carry_out,
       n1_bit_adder_4_carry_out, n1_bit_adder_5_carry_out, n1_bit_adder_6_carry_out,
       n1_bit_adder_7_carry_out, n1_bit_adder_8_carry_out, n1_bit_adder_9_carry_out,
       n1_bit_adder_10_carry_out, n1_bit_adder_11_carry_out, n1_bit_adder_12_carry_out,
       n1_bit_adder_13_carry_out, n1_bit_adder_14_carry_out, n1_bit_adder_15_carry_out,
       n1_bit_adder_16_carry_out, n1_bit_adder_17_carry_out, n1_bit_adder_18_carry_out,
       n1_bit_adder_19_carry_out, n1_bit_adder_20_carry_out, n1_bit_adder_21_carry_out,
       n1_bit_adder_22_carry_out, n1_bit_adder_23_carry_out, n1_bit_adder_24_carry_out,
       n1_bit_adder_25_carry_out, n1_bit_adder_26_carry_out, n1_bit_adder_27_carry_out,
       n1_bit_adder_28_carry_out, n1_bit_adder_29_carry_out, n1_bit_adder_30_carry_out,
       n1_bit_adder_31_carry_out, xor_1_out, xor_2_out;

  _1_bit_adder u_1_bit_adder_1 (
    .A(_32_bit_A[0]), .B(_32_bit_B[0]), .Carry(1'b0), .Sum(_32_bit_output[0]),
    .Carry_Out(n1_bit_adder_1_carry_out));
  _1_bit_adder u_1_bit_adder_2 (
    .A(_32_bit_A[1]), .B(_32_bit_B[1]), .Carry(n1_bit_adder_1_carry_out), .Sum(_32_bit_output[1]),
    .Carry_Out(n1_bit_adder_2_carry_out));
  _1_bit_adder u_1_bit_adder_3 (
    .A(_32_bit_A[2]), .B(_32_bit_B[2]), .Carry(n1_bit_adder_2_carry_out), .Sum(_32_bit_output[2]),
    .Carry_Out(n1_bit_adder_3_carry_out));
  _1_bit_adder u_1_bit_adder_4 (
    .A(_32_bit_A[3]), .B(_32_bit_B[3]), .Carry(n1_bit_adder_3_carry_out), .Sum(_32_bit_output[3]),
    .Carry_Out(n1_bit_adder_4_carry_out));
  _1_bit_adder u_1_bit_adder_5 (
    .A(_32_bit_A[4]), .B(_32_bit_B[4]), .Carry(n1_bit_adder_4_carry_out), .Sum(_32_bit_output[4]),
    .Carry_Out(n1_bit_adder_5_carry_out));
  _1_bit_adder u_1_bit_adder_6 (
    .A(_32_bit_A[5]), .B(_32_bit_B[5]), .Carry(n1_bit_adder_5_carry_out), .Sum(_32_bit_output[5]),
    .Carry_Out(n1_bit_adder_6_carry_out));
  _1_bit_adder u_1_bit_adder_7 (
    .A(_32_bit_A[6]), .B(_32_bit_B[6]), .Carry(n1_bit_adder_6_carry_out), .Sum(_32_bit_output[6]),
    .Carry_Out(n1_bit_adder_7_carry_out));
  _1_bit_adder u_1_bit_adder_8 (
    .A(_32_bit_A[7]), .B(_32_bit_B[7]), .Carry(n1_bit_adder_7_carry_out), .Sum(_32_bit_output[7]),
    .Carry_Out(n1_bit_adder_8_carry_out));
  _1_bit_adder u_1_bit_adder_9 (
    .A(_32_bit_A[8]), .B(_32_bit_B[8]), .Carry(n1_bit_adder_8_carry_out), .Sum(_32_bit_output[8]),
    .Carry_Out(n1_bit_adder_9_carry_out));
  _1_bit_adder u_1_bit_adder_10 (
    .A(_32_bit_A[9]), .B(_32_bit_B[9]), .Carry(n1_bit_adder_9_carry_out), .Sum(_32_bit_output[9]),
    .Carry_Out(n1_bit_adder_10_carry_out));
  _1_bit_adder u_1_bit_adder_11 (
    .A(_32_bit_A[10]), .B(_32_bit_B[10]), .Carry(n1_bit_adder_10_carry_out), .Sum(_32_bit_output[10]),
    .Carry_Out(n1_bit_adder_11_carry_out));
  _1_bit_adder u_1_bit_adder_12 (
    .A(_32_bit_A[11]), .B(_32_bit_B[11]), .Carry(n1_bit_adder_11_carry_out), .Sum(_32_bit_output[11]),
    .Carry_Out(n1_bit_adder_12_carry_out));
  _1_bit_adder u_1_bit_adder_13 (
    .A(_32_bit_A[12]), .B(_32_bit_B[12]), .Carry(n1_bit_adder_12_carry_out), .Sum(_32_bit_output[12]),
    .Carry_Out(n1_bit_adder_13_carry_out));
  _1_bit_adder u_1_bit_adder_14 (
    .A(_32_bit_A[13]), .B(_32_bit_B[13]), .Carry(n1_bit_adder_13_carry_out), .Sum(_32_bit_output[13]),
    .Carry_Out(n1_bit_adder_14_carry_out));
  _1_bit_adder u_1_bit_adder_15 (
    .A(_32_bit_A[14]), .B(_32_bit_B[14]), .Carry(n1_bit_adder_14_carry_out), .Sum(_32_bit_output[14]),
    .Carry_Out(n1_bit_adder_15_carry_out));
  _1_bit_adder u_1_bit_adder_16 (
    .A(_32_bit_A[15]), .B(_32_bit_B[15]), .Carry(n1_bit_adder_15_carry_out), .Sum(_32_bit_output[15]),
    .Carry_Out(n1_bit_adder_16_carry_out));
  _1_bit_adder u_1_bit_adder_17 (
    .A(_32_bit_A[16]), .B(_32_bit_B[16]), .Carry(n1_bit_adder_16_carry_out), .Sum(_32_bit_output[16]),
    .Carry_Out(n1_bit_adder_17_carry_out));
  _1_bit_adder u_1_bit_adder_18 (
    .A(_32_bit_A[17]), .B(_32_bit_B[17]), .Carry(n1_bit_adder_17_carry_out), .Sum(_32_bit_output[17]),
    .Carry_Out(n1_bit_adder_18_carry_out));
  _1_bit_adder u_1_bit_adder_19 (
    .A(_32_bit_A[18]), .B(_32_bit_B[18]), .Carry(n1_bit_adder_18_carry_out), .Sum(_32_bit_output[18]),
    .Carry_Out(n1_bit_adder_19_carry_out));
  _1_bit_adder u_1_bit_adder_20 (
    .A(_32_bit_A[19]), .B(_32_bit_B[19]), .Carry(n1_bit_adder_19_carry_out), .Sum(_32_bit_output[19]),
    .Carry_Out(n1_bit_adder_20_carry_out));
  _1_bit_adder u_1_bit_adder_21 (
    .A(_32_bit_A[20]), .B(_32_bit_B[20]), .Carry(n1_bit_adder_20_carry_out), .Sum(_32_bit_output[20]),
    .Carry_Out(n1_bit_adder_21_carry_out));
  _1_bit_adder u_1_bit_adder_22 (
    .A(_32_bit_A[21]), .B(_32_bit_B[21]), .Carry(n1_bit_adder_21_carry_out), .Sum(_32_bit_output[21]),
    .Carry_Out(n1_bit_adder_22_carry_out));
  _1_bit_adder u_1_bit_adder_23 (
    .A(_32_bit_A[22]), .B(_32_bit_B[22]), .Carry(n1_bit_adder_22_carry_out), .Sum(_32_bit_output[22]),
    .Carry_Out(n1_bit_adder_23_carry_out));
  _1_bit_adder u_1_bit_adder_24 (
    .A(_32_bit_A[23]), .B(_32_bit_B[23]), .Carry(n1_bit_adder_23_carry_out), .Sum(_32_bit_output[23]),
    .Carry_Out(n1_bit_adder_24_carry_out));
  _1_bit_adder u_1_bit_adder_25 (
    .A(_32_bit_A[24]), .B(_32_bit_B[24]), .Carry(n1_bit_adder_24_carry_out), .Sum(_32_bit_output[24]),
    .Carry_Out(n1_bit_adder_25_carry_out));
  _1_bit_adder u_1_bit_adder_26 (
    .A(_32_bit_A[25]), .B(_32_bit_B[25]), .Carry(n1_bit_adder_25_carry_out), .Sum(_32_bit_output[25]),
    .Carry_Out(n1_bit_adder_26_carry_out));
  _1_bit_adder u_1_bit_adder_27 (
    .A(_32_bit_A[26]), .B(_32_bit_B[26]), .Carry(n1_bit_adder_26_carry_out), .Sum(_32_bit_output[26]),
    .Carry_Out(n1_bit_adder_27_carry_out));
  _1_bit_adder u_1_bit_adder_28 (
    .A(_32_bit_A[27]), .B(_32_bit_B[27]), .Carry(n1_bit_adder_27_carry_out), .Sum(_32_bit_output[27]),
    .Carry_Out(n1_bit_adder_28_carry_out));
  _1_bit_adder u_1_bit_adder_29 (
    .A(_32_bit_A[28]), .B(_32_bit_B[28]), .Carry(n1_bit_adder_28_carry_out), .Sum(_32_bit_output[28]),
    .Carry_Out(n1_bit_adder_29_carry_out));
  _1_bit_adder u_1_bit_adder_30 (
    .A(_32_bit_A[29]), .B(_32_bit_B[29]), .Carry(n1_bit_adder_29_carry_out), .Sum(_32_bit_output[29]),
    .Carry_Out(n1_bit_adder_30_carry_out));
  _1_bit_adder u_1_bit_adder_31 (
    .A(_32_bit_A[30]), .B(_32_bit_B[30]), .Carry(n1_bit_adder_30_carry_out), .Sum(_32_bit_output[30]),
    .Carry_Out(n1_bit_adder_31_carry_out));
  _1_bit_adder u_1_bit_adder_32 (
    .A(_32_bit_A[31]), .B(_32_bit_B[31]), .Carry(n1_bit_adder_31_carry_out), .Sum(_32_bit_output[31]),
    .Carry_Out(carryout));
  xor xor_1 (xor_1_out, _32_bit_output[31], _32_bit_A[31]);
  xor xor_2 (xor_2_out, _32_bit_A[31], _32_bit_B[31]);
  Multiplexer #(.enable("false")) multiplexer_1 (.in0(xor_1_out), .in1(1'b0), .out(overflow), .sel(xor_2_out));
endmodule

// sub
module _32_bit_subtractor (
  input  [31:0] _32_bit_A,
  input  [31:0] _32_bit_B,
  output [31:0] _32_bit_output,
  output carryout,
  output overflow
);

  wire n1_bit_adder_1_carry_out, n1_bit_adder_2_carry_out, n1_bit_adder_3_carry_out,
       n1_bit_adder_4_carry_out, n1_bit_adder_5_carry_out, n1_bit_adder_6_carry_out,
       n1_bit_adder_7_carry_out, n1_bit_adder_8_carry_out, n1_bit_adder_9_carry_out,
       n1_bit_adder_10_carry_out, n1_bit_adder_11_carry_out, n1_bit_adder_12_carry_out,
       n1_bit_adder_13_carry_out, n1_bit_adder_14_carry_out, n1_bit_adder_15_carry_out,
       n1_bit_adder_16_carry_out, n1_bit_adder_17_carry_out, n1_bit_adder_18_carry_out,
       n1_bit_adder_19_carry_out, n1_bit_adder_20_carry_out, n1_bit_adder_21_carry_out,
       n1_bit_adder_22_carry_out, n1_bit_adder_23_carry_out, n1_bit_adder_24_carry_out,
       n1_bit_adder_25_carry_out, n1_bit_adder_26_carry_out, n1_bit_adder_27_carry_out,
       n1_bit_adder_28_carry_out, n1_bit_adder_29_carry_out, n1_bit_adder_30_carry_out,
       n1_bit_adder_31_carry_out, xor_1_out, xor_2_out;
  wire [31:0] not_1_out;

  assign not_1_out = ~_32_bit_B;  // NOT_Gate not_1, 32 bits wide
  _1_bit_adder u_1_bit_adder_1 (
    .A(_32_bit_A[0]), .B(not_1_out[0]), .Carry(1'b1), .Sum(_32_bit_output[0]),
    .Carry_Out(n1_bit_adder_1_carry_out));
  _1_bit_adder u_1_bit_adder_2 (
    .A(_32_bit_A[1]), .B(not_1_out[1]), .Carry(n1_bit_adder_1_carry_out), .Sum(_32_bit_output[1]),
    .Carry_Out(n1_bit_adder_2_carry_out));
  _1_bit_adder u_1_bit_adder_3 (
    .A(_32_bit_A[2]), .B(not_1_out[2]), .Carry(n1_bit_adder_2_carry_out), .Sum(_32_bit_output[2]),
    .Carry_Out(n1_bit_adder_3_carry_out));
  _1_bit_adder u_1_bit_adder_4 (
    .A(_32_bit_A[3]), .B(not_1_out[3]), .Carry(n1_bit_adder_3_carry_out), .Sum(_32_bit_output[3]),
    .Carry_Out(n1_bit_adder_4_carry_out));
  _1_bit_adder u_1_bit_adder_5 (
    .A(_32_bit_A[4]), .B(not_1_out[4]), .Carry(n1_bit_adder_4_carry_out), .Sum(_32_bit_output[4]),
    .Carry_Out(n1_bit_adder_5_carry_out));
  _1_bit_adder u_1_bit_adder_6 (
    .A(_32_bit_A[5]), .B(not_1_out[5]), .Carry(n1_bit_adder_5_carry_out), .Sum(_32_bit_output[5]),
    .Carry_Out(n1_bit_adder_6_carry_out));
  _1_bit_adder u_1_bit_adder_7 (
    .A(_32_bit_A[6]), .B(not_1_out[6]), .Carry(n1_bit_adder_6_carry_out), .Sum(_32_bit_output[6]),
    .Carry_Out(n1_bit_adder_7_carry_out));
  _1_bit_adder u_1_bit_adder_8 (
    .A(_32_bit_A[7]), .B(not_1_out[7]), .Carry(n1_bit_adder_7_carry_out), .Sum(_32_bit_output[7]),
    .Carry_Out(n1_bit_adder_8_carry_out));
  _1_bit_adder u_1_bit_adder_9 (
    .A(_32_bit_A[8]), .B(not_1_out[8]), .Carry(n1_bit_adder_8_carry_out), .Sum(_32_bit_output[8]),
    .Carry_Out(n1_bit_adder_9_carry_out));
  _1_bit_adder u_1_bit_adder_10 (
    .A(_32_bit_A[9]), .B(not_1_out[9]), .Carry(n1_bit_adder_9_carry_out), .Sum(_32_bit_output[9]),
    .Carry_Out(n1_bit_adder_10_carry_out));
  _1_bit_adder u_1_bit_adder_11 (
    .A(_32_bit_A[10]), .B(not_1_out[10]), .Carry(n1_bit_adder_10_carry_out), .Sum(_32_bit_output[10]),
    .Carry_Out(n1_bit_adder_11_carry_out));
  _1_bit_adder u_1_bit_adder_12 (
    .A(_32_bit_A[11]), .B(not_1_out[11]), .Carry(n1_bit_adder_11_carry_out), .Sum(_32_bit_output[11]),
    .Carry_Out(n1_bit_adder_12_carry_out));
  _1_bit_adder u_1_bit_adder_13 (
    .A(_32_bit_A[12]), .B(not_1_out[12]), .Carry(n1_bit_adder_12_carry_out), .Sum(_32_bit_output[12]),
    .Carry_Out(n1_bit_adder_13_carry_out));
  _1_bit_adder u_1_bit_adder_14 (
    .A(_32_bit_A[13]), .B(not_1_out[13]), .Carry(n1_bit_adder_13_carry_out), .Sum(_32_bit_output[13]),
    .Carry_Out(n1_bit_adder_14_carry_out));
  _1_bit_adder u_1_bit_adder_15 (
    .A(_32_bit_A[14]), .B(not_1_out[14]), .Carry(n1_bit_adder_14_carry_out), .Sum(_32_bit_output[14]),
    .Carry_Out(n1_bit_adder_15_carry_out));
  _1_bit_adder u_1_bit_adder_16 (
    .A(_32_bit_A[15]), .B(not_1_out[15]), .Carry(n1_bit_adder_15_carry_out), .Sum(_32_bit_output[15]),
    .Carry_Out(n1_bit_adder_16_carry_out));
  _1_bit_adder u_1_bit_adder_17 (
    .A(_32_bit_A[16]), .B(not_1_out[16]), .Carry(n1_bit_adder_16_carry_out), .Sum(_32_bit_output[16]),
    .Carry_Out(n1_bit_adder_17_carry_out));
  _1_bit_adder u_1_bit_adder_18 (
    .A(_32_bit_A[17]), .B(not_1_out[17]), .Carry(n1_bit_adder_17_carry_out), .Sum(_32_bit_output[17]),
    .Carry_Out(n1_bit_adder_18_carry_out));
  _1_bit_adder u_1_bit_adder_19 (
    .A(_32_bit_A[18]), .B(not_1_out[18]), .Carry(n1_bit_adder_18_carry_out), .Sum(_32_bit_output[18]),
    .Carry_Out(n1_bit_adder_19_carry_out));
  _1_bit_adder u_1_bit_adder_20 (
    .A(_32_bit_A[19]), .B(not_1_out[19]), .Carry(n1_bit_adder_19_carry_out), .Sum(_32_bit_output[19]),
    .Carry_Out(n1_bit_adder_20_carry_out));
  _1_bit_adder u_1_bit_adder_21 (
    .A(_32_bit_A[20]), .B(not_1_out[20]), .Carry(n1_bit_adder_20_carry_out), .Sum(_32_bit_output[20]),
    .Carry_Out(n1_bit_adder_21_carry_out));
  _1_bit_adder u_1_bit_adder_22 (
    .A(_32_bit_A[21]), .B(not_1_out[21]), .Carry(n1_bit_adder_21_carry_out), .Sum(_32_bit_output[21]),
    .Carry_Out(n1_bit_adder_22_carry_out));
  _1_bit_adder u_1_bit_adder_23 (
    .A(_32_bit_A[22]), .B(not_1_out[22]), .Carry(n1_bit_adder_22_carry_out), .Sum(_32_bit_output[22]),
    .Carry_Out(n1_bit_adder_23_carry_out));
  _1_bit_adder u_1_bit_adder_24 (
    .A(_32_bit_A[23]), .B(not_1_out[23]), .Carry(n1_bit_adder_23_carry_out), .Sum(_32_bit_output[23]),
    .Carry_Out(n1_bit_adder_24_carry_out));
  _1_bit_adder u_1_bit_adder_25 (
    .A(_32_bit_A[24]), .B(not_1_out[24]), .Carry(n1_bit_adder_24_carry_out), .Sum(_32_bit_output[24]),
    .Carry_Out(n1_bit_adder_25_carry_out));
  _1_bit_adder u_1_bit_adder_26 (
    .A(_32_bit_A[25]), .B(not_1_out[25]), .Carry(n1_bit_adder_25_carry_out), .Sum(_32_bit_output[25]),
    .Carry_Out(n1_bit_adder_26_carry_out));
  _1_bit_adder u_1_bit_adder_27 (
    .A(_32_bit_A[26]), .B(not_1_out[26]), .Carry(n1_bit_adder_26_carry_out), .Sum(_32_bit_output[26]),
    .Carry_Out(n1_bit_adder_27_carry_out));
  _1_bit_adder u_1_bit_adder_28 (
    .A(_32_bit_A[27]), .B(not_1_out[27]), .Carry(n1_bit_adder_27_carry_out), .Sum(_32_bit_output[27]),
    .Carry_Out(n1_bit_adder_28_carry_out));
  _1_bit_adder u_1_bit_adder_29 (
    .A(_32_bit_A[28]), .B(not_1_out[28]), .Carry(n1_bit_adder_28_carry_out), .Sum(_32_bit_output[28]),
    .Carry_Out(n1_bit_adder_29_carry_out));
  _1_bit_adder u_1_bit_adder_30 (
    .A(_32_bit_A[29]), .B(not_1_out[29]), .Carry(n1_bit_adder_29_carry_out), .Sum(_32_bit_output[29]),
    .Carry_Out(n1_bit_adder_30_carry_out));
  _1_bit_adder u_1_bit_adder_31 (
    .A(_32_bit_A[30]), .B(not_1_out[30]), .Carry(n1_bit_adder_30_carry_out), .Sum(_32_bit_output[30]),
    .Carry_Out(n1_bit_adder_31_carry_out));
  _1_bit_adder u_1_bit_adder_32 (
    .A(_32_bit_A[31]), .B(not_1_out[31]), .Carry(n1_bit_adder_31_carry_out), .Sum(_32_bit_output[31]),
    .Carry_Out(carryout));
  xor xor_1 (xor_1_out, _32_bit_output[31], _32_bit_A[31]);
  xor xor_2 (xor_2_out, _32_bit_A[31], not_1_out[31]);
  Multiplexer #(.enable("false")) multiplexer_1 (.in0(xor_1_out), .in1(1'b0), .out(overflow), .sel(xor_2_out));
endmodule

// slt
module _32_bit_set_less_than (
  input  [31:0] _32_bit_A,
  input  [31:0] _32_bit_B,
  output [31:0] _32_bit_C
);

  wire [30:0] n32_bit_subtractor_1__32_bit_output;

  _32_bit_subtractor u_32_bit_subtractor_1 (
    ._32_bit_A(_32_bit_A), ._32_bit_B(_32_bit_B),
    ._32_bit_output({_32_bit_C[0], n32_bit_subtractor_1__32_bit_output}));  // open: carryout, overflow

  assign _32_bit_C[31:1] = {31{1'b0}};
endmodule

// sll1
module _1_bit_shift_left (
  input  [31:0] _32_bit_Input,
  output [31:0] Shift_Output,
  output Overflow
);

  xor xor_1 (Overflow, _32_bit_Input[30], _32_bit_Input[31]);

  assign Shift_Output = {_32_bit_Input[30:0], 1'b0};
endmodule

// sll2
module _2_bit_shift_left (
  input  [31:0] _32_bit_input,
  output [31:0] Shift_Output,
  output Overflow
);

  wire n1_bit_shift_left_1_overflow, n1_bit_shift_left_2_overflow;
  wire [31:0] n1_bit_shift_left_2_shift_output;

  _1_bit_shift_left u_1_bit_shift_left_1 (
    ._32_bit_Input(n1_bit_shift_left_2_shift_output), .Shift_Output(Shift_Output),
    .Overflow(n1_bit_shift_left_1_overflow));
  _1_bit_shift_left u_1_bit_shift_left_2 (
    ._32_bit_Input(_32_bit_input), .Shift_Output(n1_bit_shift_left_2_shift_output),
    .Overflow(n1_bit_shift_left_2_overflow));
  or or_1 (Overflow, n1_bit_shift_left_1_overflow, n1_bit_shift_left_2_overflow);
endmodule

// sll4
module _4_bit_shift_left (
  input  [31:0] _32_bit_input,
  output [31:0] Shift_Output,
  output Overflow
);

  wire n2_bit_shift_left_1_overflow, n2_bit_shift_left_2_overflow;
  wire [31:0] n2_bit_shift_left_2_shift_output;

  _2_bit_shift_left u_2_bit_shift_left_1 (
    ._32_bit_input(n2_bit_shift_left_2_shift_output), .Shift_Output(Shift_Output),
    .Overflow(n2_bit_shift_left_1_overflow));
  _2_bit_shift_left u_2_bit_shift_left_2 (
    ._32_bit_input(_32_bit_input), .Shift_Output(n2_bit_shift_left_2_shift_output),
    .Overflow(n2_bit_shift_left_2_overflow));
  or or_1 (Overflow, n2_bit_shift_left_1_overflow, n2_bit_shift_left_2_overflow);
endmodule

// sll8
module _8_bit_shift_left (
  input  [31:0] _32_bit_input,
  output [31:0] Shift_Output,
  output Overflow
);

  wire n4_bit_shift_left_1_overflow, n4_bit_shift_left_2_overflow;
  wire [31:0] n4_bit_shift_left_1_shift_output;

  _4_bit_shift_left u_4_bit_shift_left_1 (
    ._32_bit_input(_32_bit_input), .Shift_Output(n4_bit_shift_left_1_shift_output),
    .Overflow(n4_bit_shift_left_1_overflow));
  _4_bit_shift_left u_4_bit_shift_left_2 (
    ._32_bit_input(n4_bit_shift_left_1_shift_output), .Shift_Output(Shift_Output),
    .Overflow(n4_bit_shift_left_2_overflow));
  or or_1 (Overflow, n4_bit_shift_left_2_overflow, n4_bit_shift_left_1_overflow);
endmodule

// sll16
module _16_bit_shift_left (
  input  [31:0] _32_bit_input,
  output [31:0] Shift_Output,
  output Overflow
);

  wire n8_bit_shift_left_1_overflow, n8_bit_shift_left_2_overflow;
  wire [31:0] n8_bit_shift_left_1_shift_output;

  _8_bit_shift_left u_8_bit_shift_left_1 (
    ._32_bit_input(_32_bit_input), .Shift_Output(n8_bit_shift_left_1_shift_output),
    .Overflow(n8_bit_shift_left_1_overflow));
  _8_bit_shift_left u_8_bit_shift_left_2 (
    ._32_bit_input(n8_bit_shift_left_1_shift_output), .Shift_Output(Shift_Output),
    .Overflow(n8_bit_shift_left_2_overflow));
  or or_1 (Overflow, n8_bit_shift_left_2_overflow, n8_bit_shift_left_1_overflow);
endmodule

// sll
module _32_bit_shift_left (
  input  [31:0] _32_bit_A,
  input  [4:0] B,
  output [31:0] _32_bit_C,
  output overflow
);

  wire and_1_out, and_2_out, and_3_out, and_4_out, and_5_out, n1_bit_shift_left_1_overflow,
       n2_bit_shift_left_1_overflow, n4_bit_shift_left_1_overflow, n8_bit_shift_left_1_overflow,
       n16_bit_shift_left_1_overflow;
  wire [31:0] multiplexer_1_out, multiplexer_2_out, multiplexer_3_out, multiplexer_4_out,
       n1_bit_shift_left_1_shift_output, n2_bit_shift_left_1_shift_output, n4_bit_shift_left_1_shift_output,
       n8_bit_shift_left_1_shift_output, n16_bit_shift_left_1_shift_output;

  _16_bit_shift_left u_16_bit_shift_left_1 (
    ._32_bit_input(_32_bit_A), .Shift_Output(n16_bit_shift_left_1_shift_output),
    .Overflow(n16_bit_shift_left_1_overflow));
  and and_1 (and_1_out, n16_bit_shift_left_1_overflow, B[4]);
  Multiplexer #(.width(32), .enable("false")) multiplexer_1 (
    .in0(_32_bit_A), .in1(n16_bit_shift_left_1_shift_output), .out(multiplexer_1_out), .sel(B[4]));
  _8_bit_shift_left u_8_bit_shift_left_1 (
    ._32_bit_input(multiplexer_1_out), .Shift_Output(n8_bit_shift_left_1_shift_output),
    .Overflow(n8_bit_shift_left_1_overflow));
  and and_2 (and_2_out, n8_bit_shift_left_1_overflow, B[3]);
  Multiplexer #(.width(32), .enable("false")) multiplexer_2 (
    .in0(multiplexer_1_out), .in1(n8_bit_shift_left_1_shift_output), .out(multiplexer_2_out), .sel(B[3]));
  _4_bit_shift_left u_4_bit_shift_left_1 (
    ._32_bit_input(multiplexer_2_out), .Shift_Output(n4_bit_shift_left_1_shift_output),
    .Overflow(n4_bit_shift_left_1_overflow));
  and and_3 (and_3_out, n4_bit_shift_left_1_overflow, B[2]);
  Multiplexer #(.width(32), .enable("false")) multiplexer_3 (
    .in0(multiplexer_2_out), .in1(n4_bit_shift_left_1_shift_output), .out(multiplexer_3_out), .sel(B[2]));
  _2_bit_shift_left u_2_bit_shift_left_1 (
    ._32_bit_input(multiplexer_3_out), .Shift_Output(n2_bit_shift_left_1_shift_output),
    .Overflow(n2_bit_shift_left_1_overflow));
  and and_4 (and_4_out, B[1], n2_bit_shift_left_1_overflow);
  Multiplexer #(.width(32), .enable("false")) multiplexer_4 (
    .in0(multiplexer_3_out), .in1(n2_bit_shift_left_1_shift_output), .out(multiplexer_4_out), .sel(B[1]));
  Multiplexer #(.width(32), .enable("false")) multiplexer_5 (
    .in0(multiplexer_4_out), .in1(n1_bit_shift_left_1_shift_output), .out(_32_bit_C), .sel(B[0]));
  _1_bit_shift_left u_1_bit_shift_left_1 (
    ._32_bit_Input(multiplexer_4_out), .Shift_Output(n1_bit_shift_left_1_shift_output),
    .Overflow(n1_bit_shift_left_1_overflow));
  and and_5 (and_5_out, n1_bit_shift_left_1_overflow, B[0]);
  or or_1 (overflow, and_5_out, and_4_out, and_3_out, and_2_out, and_1_out);
endmodule

// srl1
module _1_bit_shift_right (
  input  [31:0] _32_bit_Input,
  output [31:0] Shift_Output
);


  assign Shift_Output = {1'b0, _32_bit_Input[31:1]};
endmodule

// srl2
module _2_bit_shift_right (
  input  [31:0] _32_bit_input,
  output [31:0] Shift_Output
);

  wire [31:0] n1_bit_shift_right_1_shift_output;

  _1_bit_shift_right u_1_bit_shift_right_1 (
    ._32_bit_Input(_32_bit_input), .Shift_Output(n1_bit_shift_right_1_shift_output));
  _1_bit_shift_right u_1_bit_shift_right_2 (
    ._32_bit_Input(n1_bit_shift_right_1_shift_output), .Shift_Output(Shift_Output));
endmodule

// srl4
module _4_bit_shift_right (
  input  [31:0] _32_bit_input,
  output [31:0] Shift_Output
);

  wire [31:0] n2_bit_shift_right_1_shift_output;

  _2_bit_shift_right u_2_bit_shift_right_1 (
    ._32_bit_input(_32_bit_input), .Shift_Output(n2_bit_shift_right_1_shift_output));
  _2_bit_shift_right u_2_bit_shift_right_2 (
    ._32_bit_input(n2_bit_shift_right_1_shift_output), .Shift_Output(Shift_Output));
endmodule

// srl8
module _8_bit_shift_right (
  input  [31:0] _32_bit_input,
  output [31:0] Shift_Output
);

  wire [31:0] n4_bit_shift_right_1_shift_output;

  _4_bit_shift_right u_4_bit_shift_right_1 (
    ._32_bit_input(_32_bit_input), .Shift_Output(n4_bit_shift_right_1_shift_output));
  _4_bit_shift_right u_4_bit_shift_right_2 (
    ._32_bit_input(n4_bit_shift_right_1_shift_output), .Shift_Output(Shift_Output));
endmodule

// srl16
module _16_bit_shift_right (
  input  [31:0] _32_bit_input,
  output [31:0] Shift_Output
);

  wire [31:0] n8_bit_shift_right_1_shift_output;

  _8_bit_shift_right u_8_bit_shift_right_1 (
    ._32_bit_input(_32_bit_input), .Shift_Output(n8_bit_shift_right_1_shift_output));
  _8_bit_shift_right u_8_bit_shift_right_2 (
    ._32_bit_input(n8_bit_shift_right_1_shift_output), .Shift_Output(Shift_Output));
endmodule

// srl
module _32_bit_shift_right (
  input  [31:0] _32_bit_A,
  input  [4:0] B,
  output [31:0] _32_bit_C
);

  wire [31:0] multiplexer_1_out, multiplexer_2_out, multiplexer_3_out, multiplexer_4_out,
       n1_bit_shift_right_1_shift_output, n2_bit_shift_right_1_shift_output,
       n4_bit_shift_right_1_shift_output, n8_bit_shift_right_1_shift_output,
       n16_bit_shift_right_1_shift_output;

  _16_bit_shift_right u_16_bit_shift_right_1 (
    ._32_bit_input(_32_bit_A), .Shift_Output(n16_bit_shift_right_1_shift_output));
  Multiplexer #(.width(32)) multiplexer_1 (
    .in0(_32_bit_A), .in1(n16_bit_shift_right_1_shift_output), .out(multiplexer_1_out), .sel(B[4]));  // open: en
  Multiplexer #(.width(32)) multiplexer_2 (
    .in0(multiplexer_1_out), .in1(n8_bit_shift_right_1_shift_output), .out(multiplexer_2_out), .sel(B[3]));  // open: en
  _8_bit_shift_right u_8_bit_shift_right_1 (
    ._32_bit_input(multiplexer_1_out), .Shift_Output(n8_bit_shift_right_1_shift_output));
  _4_bit_shift_right u_4_bit_shift_right_1 (
    ._32_bit_input(multiplexer_2_out), .Shift_Output(n4_bit_shift_right_1_shift_output));
  Multiplexer #(.width(32)) multiplexer_3 (
    .in0(multiplexer_2_out), .in1(n4_bit_shift_right_1_shift_output), .out(multiplexer_3_out), .sel(B[2]));  // open: en
  Multiplexer #(.width(32)) multiplexer_4 (
    .in0(multiplexer_3_out), .in1(n2_bit_shift_right_1_shift_output), .out(multiplexer_4_out), .sel(B[1]));  // open: en
  _2_bit_shift_right u_2_bit_shift_right_1 (
    ._32_bit_input(multiplexer_3_out), .Shift_Output(n2_bit_shift_right_1_shift_output));
  _1_bit_shift_right u_1_bit_shift_right_1 (
    ._32_bit_Input(multiplexer_4_out), .Shift_Output(n1_bit_shift_right_1_shift_output));
  Multiplexer #(.width(32)) multiplexer_5 (
    .in0(multiplexer_4_out), .in1(n1_bit_shift_right_1_shift_output), .out(_32_bit_C), .sel(B[0]));  // open: en
endmodule

// sra1
module _1_bit_shift_right_arithmatic (
  input  [31:0] _32_bit_input,
  output [31:0] Shift_Output
);


  assign Shift_Output = {{2{_32_bit_input[31]}}, _32_bit_input[30:1]};
endmodule

// sra2
module _2_bit_shift_right_arithmatic (
  input  [31:0] _32_bit_input,
  output [31:0] Shift_Output
);

  wire [31:0] n1_bit_shift_right_arithmatic_1_shift_output;

  _1_bit_shift_right_arithmatic u_1_bit_shift_right_arithmatic_1 (
    ._32_bit_input(_32_bit_input), .Shift_Output(n1_bit_shift_right_arithmatic_1_shift_output));
  _1_bit_shift_right_arithmatic u_1_bit_shift_right_arithmatic_2 (
    ._32_bit_input(n1_bit_shift_right_arithmatic_1_shift_output), .Shift_Output(Shift_Output));
endmodule

// sra4
module _4_bit_shift_right_arithmatic (
  input  [31:0] _32_bit_input,
  output [31:0] Shift_Output
);

  wire [31:0] n2_bit_shift_right_arithmatic_1_shift_output;

  _2_bit_shift_right_arithmatic u_2_bit_shift_right_arithmatic_1 (
    ._32_bit_input(_32_bit_input), .Shift_Output(n2_bit_shift_right_arithmatic_1_shift_output));
  _2_bit_shift_right_arithmatic u_2_bit_shift_right_arithmatic_2 (
    ._32_bit_input(n2_bit_shift_right_arithmatic_1_shift_output), .Shift_Output(Shift_Output));
endmodule

// sra8
module _8_bit_shift_right_arithmatic (
  input  [31:0] _32_bit_input,
  output [31:0] Shift_Output
);

  wire [31:0] n4_bit_shift_right_arithmatic_1_shift_output;

  _4_bit_shift_right_arithmatic u_4_bit_shift_right_arithmatic_1 (
    ._32_bit_input(_32_bit_input), .Shift_Output(n4_bit_shift_right_arithmatic_1_shift_output));
  _4_bit_shift_right_arithmatic u_4_bit_shift_right_arithmatic_2 (
    ._32_bit_input(n4_bit_shift_right_arithmatic_1_shift_output), .Shift_Output(Shift_Output));
endmodule

// sra16
module _16_bit_shift_right_arithmatic (
  input  [31:0] _32_bit_input,
  output [31:0] Shift_Output
);

  wire [31:0] n8_bit_shift_right_arithmatic_1_shift_output;

  _8_bit_shift_right_arithmatic u_8_bit_shift_right_arithmatic_1 (
    ._32_bit_input(_32_bit_input), .Shift_Output(n8_bit_shift_right_arithmatic_1_shift_output));
  _8_bit_shift_right_arithmatic u_8_bit_shift_right_arithmatic_2 (
    ._32_bit_input(n8_bit_shift_right_arithmatic_1_shift_output), .Shift_Output(Shift_Output));
endmodule

// sra
module _32_bit_shift_right_arithmatic (
  input  [31:0] _32_bit_A,
  input  [4:0] B,
  output [31:0] _32_bit_C
);

  wire [31:0] multiplexer_1_out, multiplexer_2_out, multiplexer_3_out, multiplexer_4_out,
       n1_bit_shift_right_arithmatic_1_shift_output, n2_bit_shift_right_arithmatic_1_shift_output,
       n4_bit_shift_right_arithmatic_1_shift_output, n8_bit_shift_right_arithmatic_1_shift_output,
       n16_bit_shift_right_arithmatic_1_shift_output;

  _16_bit_shift_right_arithmatic u_16_bit_shift_right_arithmatic_1 (
    ._32_bit_input(_32_bit_A), .Shift_Output(n16_bit_shift_right_arithmatic_1_shift_output));
  Multiplexer #(.width(32), .enable("false")) multiplexer_1 (
    .in0(_32_bit_A), .in1(n16_bit_shift_right_arithmatic_1_shift_output), .out(multiplexer_1_out), .sel(B[4]));
  Multiplexer #(.width(32), .enable("false")) multiplexer_2 (
    .in0(multiplexer_1_out), .in1(n8_bit_shift_right_arithmatic_1_shift_output), .out(multiplexer_2_out),
    .sel(B[3]));
  _8_bit_shift_right_arithmatic u_8_bit_shift_right_arithmatic_1 (
    ._32_bit_input(multiplexer_1_out), .Shift_Output(n8_bit_shift_right_arithmatic_1_shift_output));
  _4_bit_shift_right_arithmatic u_4_bit_shift_right_arithmatic_1 (
    ._32_bit_input(multiplexer_2_out), .Shift_Output(n4_bit_shift_right_arithmatic_1_shift_output));
  Multiplexer #(.width(32), .enable("false")) multiplexer_3 (
    .in0(multiplexer_2_out), .in1(n4_bit_shift_right_arithmatic_1_shift_output), .out(multiplexer_3_out),
    .sel(B[2]));
  Multiplexer #(.width(32), .enable("false")) multiplexer_4 (
    .in0(multiplexer_3_out), .in1(n2_bit_shift_right_arithmatic_1_shift_output), .out(multiplexer_4_out),
    .sel(B[1]));
  _2_bit_shift_right_arithmatic u_2_bit_shift_right_arithmatic_1 (
    ._32_bit_input(multiplexer_3_out), .Shift_Output(n2_bit_shift_right_arithmatic_1_shift_output));
  _1_bit_shift_right_arithmatic u_1_bit_shift_right_arithmatic_1 (
    ._32_bit_input(multiplexer_4_out), .Shift_Output(n1_bit_shift_right_arithmatic_1_shift_output));
  Multiplexer #(.width(32), .enable("false")) multiplexer_5 (
    .in0(multiplexer_4_out), .in1(n1_bit_shift_right_arithmatic_1_shift_output), .out(_32_bit_C), .sel(B[0]));
endmodule

// add8
module _8_bit_adder (
  input  [7:0] _8_bit_A,
  input  [7:0] _8_bit_B,
  output [7:0] _8_bit_Output,
  output Cout
);

  wire n1_bit_adder_1_carry_out, n1_bit_adder_2_carry_out, n1_bit_adder_3_carry_out,
       n1_bit_adder_4_carry_out, n1_bit_adder_5_carry_out, n1_bit_adder_6_carry_out, n1_bit_adder_7_carry_out;

  _1_bit_adder u_1_bit_adder_1 (
    .A(_8_bit_A[0]), .B(_8_bit_B[0]), .Carry(1'b0), .Sum(_8_bit_Output[0]),
    .Carry_Out(n1_bit_adder_1_carry_out));
  _1_bit_adder u_1_bit_adder_2 (
    .A(_8_bit_A[1]), .B(_8_bit_B[1]), .Carry(n1_bit_adder_1_carry_out), .Sum(_8_bit_Output[1]),
    .Carry_Out(n1_bit_adder_2_carry_out));
  _1_bit_adder u_1_bit_adder_3 (
    .A(_8_bit_A[2]), .B(_8_bit_B[2]), .Carry(n1_bit_adder_2_carry_out), .Sum(_8_bit_Output[2]),
    .Carry_Out(n1_bit_adder_3_carry_out));
  _1_bit_adder u_1_bit_adder_4 (
    .A(_8_bit_A[3]), .B(_8_bit_B[3]), .Carry(n1_bit_adder_3_carry_out), .Sum(_8_bit_Output[3]),
    .Carry_Out(n1_bit_adder_4_carry_out));
  _1_bit_adder u_1_bit_adder_5 (
    .A(_8_bit_A[4]), .B(_8_bit_B[4]), .Carry(n1_bit_adder_4_carry_out), .Sum(_8_bit_Output[4]),
    .Carry_Out(n1_bit_adder_5_carry_out));
  _1_bit_adder u_1_bit_adder_6 (
    .A(_8_bit_A[5]), .B(_8_bit_B[5]), .Carry(n1_bit_adder_5_carry_out), .Sum(_8_bit_Output[5]),
    .Carry_Out(n1_bit_adder_6_carry_out));
  _1_bit_adder u_1_bit_adder_7 (
    .A(_8_bit_A[6]), .B(_8_bit_B[6]), .Carry(n1_bit_adder_6_carry_out), .Sum(_8_bit_Output[6]),
    .Carry_Out(n1_bit_adder_7_carry_out));
  _1_bit_adder u_1_bit_adder_8 (
    .A(_8_bit_A[7]), .B(_8_bit_B[7]), .Carry(n1_bit_adder_7_carry_out), .Sum(_8_bit_Output[7]),
    .Carry_Out(Cout));
endmodule

// m1
module _16_bit_mult_with_1_bit (
  input  [15:0] _16_bit_A,
  input  _1_bit_of_B,
  output [15:0] _16_bit_output
);

  assign _16_bit_output = _16_bit_A & {16{_1_bit_of_B}};  // AND_Gate and_1, 16 bits wide
endmodule

// mult
module _16_to_32_bit_multiplier (
  input  [15:0] _16_bit_A,
  input  [15:0] _16_bit_B,
  output [31:0] _32_bit_C
);

  wire [15:0] n16_bit_mult_with_1_bit_2__16_bit_output, n16_bit_mult_with_1_bit_3__16_bit_output,
       n16_bit_mult_with_1_bit_4__16_bit_output, n16_bit_mult_with_1_bit_5__16_bit_output,
       n16_bit_mult_with_1_bit_6__16_bit_output, n16_bit_mult_with_1_bit_7__16_bit_output,
       n16_bit_mult_with_1_bit_8__16_bit_output, n16_bit_mult_with_1_bit_9__16_bit_output,
       n16_bit_mult_with_1_bit_10__16_bit_output, n16_bit_mult_with_1_bit_11__16_bit_output,
       n16_bit_mult_with_1_bit_12__16_bit_output, n16_bit_mult_with_1_bit_13__16_bit_output,
       n16_bit_mult_with_1_bit_14__16_bit_output, n16_bit_mult_with_1_bit_15__16_bit_output,
       n16_bit_mult_with_1_bit_16__16_bit_output;
  wire [15:1] n16_bit_adder_1__32_bit_output, n16_bit_adder_2__32_bit_output, n16_bit_adder_3__32_bit_output,
       n16_bit_adder_4__32_bit_output, n16_bit_adder_5__32_bit_output, n16_bit_adder_6__32_bit_output,
       n16_bit_adder_7__32_bit_output, n16_bit_adder_8__32_bit_output, n16_bit_adder_9__32_bit_output,
       n16_bit_adder_10__32_bit_output, n16_bit_adder_11__32_bit_output, n16_bit_adder_12__32_bit_output,
       n16_bit_adder_13__32_bit_output, n16_bit_adder_14__32_bit_output,
       n16_bit_mult_with_1_bit_1__16_bit_output;
  wire [15:15] n16_bit_adder_1_carryout, n16_bit_adder_2_carryout, n16_bit_adder_3_carryout,
       n16_bit_adder_4_carryout, n16_bit_adder_5_carryout, n16_bit_adder_6_carryout,
       n16_bit_adder_7_carryout, n16_bit_adder_8_carryout, n16_bit_adder_9_carryout,
       n16_bit_adder_10_carryout, n16_bit_adder_11_carryout, n16_bit_adder_12_carryout,
       n16_bit_adder_13_carryout, n16_bit_adder_14_carryout;

  _16_bit_mult_with_1_bit u_16_bit_mult_with_1_bit_1 (
    ._16_bit_A(_16_bit_A), ._1_bit_of_B(_16_bit_B[0]),
    ._16_bit_output({n16_bit_mult_with_1_bit_1__16_bit_output, _32_bit_C[0]}));
  _16_bit_mult_with_1_bit u_16_bit_mult_with_1_bit_2 (
    ._16_bit_A(_16_bit_A), ._1_bit_of_B(_16_bit_B[1]),
    ._16_bit_output(n16_bit_mult_with_1_bit_2__16_bit_output));
  _16_bit_mult_with_1_bit u_16_bit_mult_with_1_bit_3 (
    ._16_bit_A(_16_bit_A), ._1_bit_of_B(_16_bit_B[2]),
    ._16_bit_output(n16_bit_mult_with_1_bit_3__16_bit_output));
  _16_bit_mult_with_1_bit u_16_bit_mult_with_1_bit_4 (
    ._16_bit_A(_16_bit_A), ._1_bit_of_B(_16_bit_B[3]),
    ._16_bit_output(n16_bit_mult_with_1_bit_4__16_bit_output));
  _16_bit_mult_with_1_bit u_16_bit_mult_with_1_bit_5 (
    ._16_bit_A(_16_bit_A), ._1_bit_of_B(_16_bit_B[4]),
    ._16_bit_output(n16_bit_mult_with_1_bit_5__16_bit_output));
  _16_bit_mult_with_1_bit u_16_bit_mult_with_1_bit_6 (
    ._16_bit_A(_16_bit_A), ._1_bit_of_B(_16_bit_B[5]),
    ._16_bit_output(n16_bit_mult_with_1_bit_6__16_bit_output));
  _16_bit_mult_with_1_bit u_16_bit_mult_with_1_bit_7 (
    ._16_bit_A(_16_bit_A), ._1_bit_of_B(_16_bit_B[6]),
    ._16_bit_output(n16_bit_mult_with_1_bit_7__16_bit_output));
  _16_bit_mult_with_1_bit u_16_bit_mult_with_1_bit_8 (
    ._16_bit_A(_16_bit_A), ._1_bit_of_B(_16_bit_B[7]),
    ._16_bit_output(n16_bit_mult_with_1_bit_8__16_bit_output));
  _16_bit_mult_with_1_bit u_16_bit_mult_with_1_bit_9 (
    ._16_bit_A(_16_bit_A), ._1_bit_of_B(_16_bit_B[8]),
    ._16_bit_output(n16_bit_mult_with_1_bit_9__16_bit_output));
  _16_bit_mult_with_1_bit u_16_bit_mult_with_1_bit_10 (
    ._16_bit_A(_16_bit_A), ._1_bit_of_B(_16_bit_B[9]),
    ._16_bit_output(n16_bit_mult_with_1_bit_10__16_bit_output));
  _16_bit_mult_with_1_bit u_16_bit_mult_with_1_bit_11 (
    ._16_bit_A(_16_bit_A), ._1_bit_of_B(_16_bit_B[10]),
    ._16_bit_output(n16_bit_mult_with_1_bit_11__16_bit_output));
  _16_bit_mult_with_1_bit u_16_bit_mult_with_1_bit_12 (
    ._16_bit_A(_16_bit_A), ._1_bit_of_B(_16_bit_B[11]),
    ._16_bit_output(n16_bit_mult_with_1_bit_12__16_bit_output));
  _16_bit_mult_with_1_bit u_16_bit_mult_with_1_bit_13 (
    ._16_bit_A(_16_bit_A), ._1_bit_of_B(_16_bit_B[12]),
    ._16_bit_output(n16_bit_mult_with_1_bit_13__16_bit_output));
  _16_bit_mult_with_1_bit u_16_bit_mult_with_1_bit_14 (
    ._16_bit_A(_16_bit_A), ._1_bit_of_B(_16_bit_B[13]),
    ._16_bit_output(n16_bit_mult_with_1_bit_14__16_bit_output));
  _16_bit_mult_with_1_bit u_16_bit_mult_with_1_bit_15 (
    ._16_bit_A(_16_bit_A), ._1_bit_of_B(_16_bit_B[14]),
    ._16_bit_output(n16_bit_mult_with_1_bit_15__16_bit_output));
  _16_bit_mult_with_1_bit u_16_bit_mult_with_1_bit_16 (
    ._16_bit_A(_16_bit_A), ._1_bit_of_B(_16_bit_B[15]),
    ._16_bit_output(n16_bit_mult_with_1_bit_16__16_bit_output));
  _16_bit_adder u_16_bit_adder_1 (
    ._16_bit_A({1'b0, n16_bit_mult_with_1_bit_1__16_bit_output}),
    ._16_bit_B(n16_bit_mult_with_1_bit_2__16_bit_output),
    ._32_bit_output({n16_bit_adder_1__32_bit_output, _32_bit_C[1]}), .Carryout(n16_bit_adder_1_carryout[15]));
  _16_bit_adder u_16_bit_adder_2 (
    ._16_bit_A({n16_bit_adder_1_carryout[15], n16_bit_adder_1__32_bit_output}),
    ._16_bit_B(n16_bit_mult_with_1_bit_3__16_bit_output),
    ._32_bit_output({n16_bit_adder_2__32_bit_output, _32_bit_C[2]}), .Carryout(n16_bit_adder_2_carryout[15]));
  _16_bit_adder u_16_bit_adder_3 (
    ._16_bit_A({n16_bit_adder_2_carryout[15], n16_bit_adder_2__32_bit_output}),
    ._16_bit_B(n16_bit_mult_with_1_bit_4__16_bit_output),
    ._32_bit_output({n16_bit_adder_3__32_bit_output, _32_bit_C[3]}), .Carryout(n16_bit_adder_3_carryout[15]));
  _16_bit_adder u_16_bit_adder_4 (
    ._16_bit_A({n16_bit_adder_3_carryout[15], n16_bit_adder_3__32_bit_output}),
    ._16_bit_B(n16_bit_mult_with_1_bit_5__16_bit_output),
    ._32_bit_output({n16_bit_adder_4__32_bit_output, _32_bit_C[4]}), .Carryout(n16_bit_adder_4_carryout[15]));
  _16_bit_adder u_16_bit_adder_5 (
    ._16_bit_A({n16_bit_adder_4_carryout[15], n16_bit_adder_4__32_bit_output}),
    ._16_bit_B(n16_bit_mult_with_1_bit_6__16_bit_output),
    ._32_bit_output({n16_bit_adder_5__32_bit_output, _32_bit_C[5]}), .Carryout(n16_bit_adder_5_carryout[15]));
  _16_bit_adder u_16_bit_adder_6 (
    ._16_bit_A({n16_bit_adder_5_carryout[15], n16_bit_adder_5__32_bit_output}),
    ._16_bit_B(n16_bit_mult_with_1_bit_7__16_bit_output),
    ._32_bit_output({n16_bit_adder_6__32_bit_output, _32_bit_C[6]}), .Carryout(n16_bit_adder_6_carryout[15]));
  _16_bit_adder u_16_bit_adder_7 (
    ._16_bit_A({n16_bit_adder_6_carryout[15], n16_bit_adder_6__32_bit_output}),
    ._16_bit_B(n16_bit_mult_with_1_bit_8__16_bit_output),
    ._32_bit_output({n16_bit_adder_7__32_bit_output, _32_bit_C[7]}), .Carryout(n16_bit_adder_7_carryout[15]));
  _16_bit_adder u_16_bit_adder_8 (
    ._16_bit_A({n16_bit_adder_7_carryout[15], n16_bit_adder_7__32_bit_output}),
    ._16_bit_B(n16_bit_mult_with_1_bit_9__16_bit_output),
    ._32_bit_output({n16_bit_adder_8__32_bit_output, _32_bit_C[8]}), .Carryout(n16_bit_adder_8_carryout[15]));
  _16_bit_adder u_16_bit_adder_9 (
    ._16_bit_A({n16_bit_adder_8_carryout[15], n16_bit_adder_8__32_bit_output}),
    ._16_bit_B(n16_bit_mult_with_1_bit_10__16_bit_output),
    ._32_bit_output({n16_bit_adder_9__32_bit_output, _32_bit_C[9]}), .Carryout(n16_bit_adder_9_carryout[15]));
  _16_bit_adder u_16_bit_adder_10 (
    ._16_bit_A({n16_bit_adder_9_carryout[15], n16_bit_adder_9__32_bit_output}),
    ._16_bit_B(n16_bit_mult_with_1_bit_11__16_bit_output),
    ._32_bit_output({n16_bit_adder_10__32_bit_output, _32_bit_C[10]}),
    .Carryout(n16_bit_adder_10_carryout[15]));
  _16_bit_adder u_16_bit_adder_11 (
    ._16_bit_A({n16_bit_adder_10_carryout[15], n16_bit_adder_10__32_bit_output}),
    ._16_bit_B(n16_bit_mult_with_1_bit_12__16_bit_output),
    ._32_bit_output({n16_bit_adder_11__32_bit_output, _32_bit_C[11]}),
    .Carryout(n16_bit_adder_11_carryout[15]));
  _16_bit_adder u_16_bit_adder_12 (
    ._16_bit_A({n16_bit_adder_11_carryout[15], n16_bit_adder_11__32_bit_output}),
    ._16_bit_B(n16_bit_mult_with_1_bit_13__16_bit_output),
    ._32_bit_output({n16_bit_adder_12__32_bit_output, _32_bit_C[12]}),
    .Carryout(n16_bit_adder_12_carryout[15]));
  _16_bit_adder u_16_bit_adder_13 (
    ._16_bit_A({n16_bit_adder_12_carryout[15], n16_bit_adder_12__32_bit_output}),
    ._16_bit_B(n16_bit_mult_with_1_bit_14__16_bit_output),
    ._32_bit_output({n16_bit_adder_13__32_bit_output, _32_bit_C[13]}),
    .Carryout(n16_bit_adder_13_carryout[15]));
  _16_bit_adder u_16_bit_adder_14 (
    ._16_bit_A({n16_bit_adder_13_carryout[15], n16_bit_adder_13__32_bit_output}),
    ._16_bit_B(n16_bit_mult_with_1_bit_15__16_bit_output),
    ._32_bit_output({n16_bit_adder_14__32_bit_output, _32_bit_C[14]}),
    .Carryout(n16_bit_adder_14_carryout[15]));
  _16_bit_adder u_16_bit_adder_15 (
    ._16_bit_A({n16_bit_adder_14_carryout[15], n16_bit_adder_14__32_bit_output}),
    ._16_bit_B(n16_bit_mult_with_1_bit_16__16_bit_output), ._32_bit_output(_32_bit_C[30:15]),
    .Carryout(_32_bit_C[31]));
endmodule

// add16
module _16_bit_adder (
  input  [15:0] _16_bit_A,
  input  [15:0] _16_bit_B,
  output [15:0] _32_bit_output,
  output Carryout
);

  wire n1_bit_adder_1_carry_out, n1_bit_adder_2_carry_out, n1_bit_adder_3_carry_out,
       n1_bit_adder_4_carry_out, n1_bit_adder_5_carry_out, n1_bit_adder_6_carry_out,
       n1_bit_adder_7_carry_out, n1_bit_adder_8_carry_out, n1_bit_adder_9_carry_out,
       n1_bit_adder_10_carry_out, n1_bit_adder_11_carry_out, n1_bit_adder_12_carry_out,
       n1_bit_adder_13_carry_out, n1_bit_adder_14_carry_out, n1_bit_adder_15_carry_out;

  _1_bit_adder u_1_bit_adder_1 (
    .A(_16_bit_A[0]), .B(_16_bit_B[0]), .Carry(1'b0), .Sum(_32_bit_output[0]),
    .Carry_Out(n1_bit_adder_1_carry_out));
  _1_bit_adder u_1_bit_adder_2 (
    .A(_16_bit_A[1]), .B(_16_bit_B[1]), .Carry(n1_bit_adder_1_carry_out), .Sum(_32_bit_output[1]),
    .Carry_Out(n1_bit_adder_2_carry_out));
  _1_bit_adder u_1_bit_adder_3 (
    .A(_16_bit_A[2]), .B(_16_bit_B[2]), .Carry(n1_bit_adder_2_carry_out), .Sum(_32_bit_output[2]),
    .Carry_Out(n1_bit_adder_3_carry_out));
  _1_bit_adder u_1_bit_adder_4 (
    .A(_16_bit_A[3]), .B(_16_bit_B[3]), .Carry(n1_bit_adder_3_carry_out), .Sum(_32_bit_output[3]),
    .Carry_Out(n1_bit_adder_4_carry_out));
  _1_bit_adder u_1_bit_adder_5 (
    .A(_16_bit_A[4]), .B(_16_bit_B[4]), .Carry(n1_bit_adder_4_carry_out), .Sum(_32_bit_output[4]),
    .Carry_Out(n1_bit_adder_5_carry_out));
  _1_bit_adder u_1_bit_adder_6 (
    .A(_16_bit_A[5]), .B(_16_bit_B[5]), .Carry(n1_bit_adder_5_carry_out), .Sum(_32_bit_output[5]),
    .Carry_Out(n1_bit_adder_6_carry_out));
  _1_bit_adder u_1_bit_adder_7 (
    .A(_16_bit_A[6]), .B(_16_bit_B[6]), .Carry(n1_bit_adder_6_carry_out), .Sum(_32_bit_output[6]),
    .Carry_Out(n1_bit_adder_7_carry_out));
  _1_bit_adder u_1_bit_adder_8 (
    .A(_16_bit_A[7]), .B(_16_bit_B[7]), .Carry(n1_bit_adder_7_carry_out), .Sum(_32_bit_output[7]),
    .Carry_Out(n1_bit_adder_8_carry_out));
  _1_bit_adder u_1_bit_adder_9 (
    .A(_16_bit_A[8]), .B(_16_bit_B[8]), .Carry(n1_bit_adder_8_carry_out), .Sum(_32_bit_output[8]),
    .Carry_Out(n1_bit_adder_9_carry_out));
  _1_bit_adder u_1_bit_adder_10 (
    .A(_16_bit_A[9]), .B(_16_bit_B[9]), .Carry(n1_bit_adder_9_carry_out), .Sum(_32_bit_output[9]),
    .Carry_Out(n1_bit_adder_10_carry_out));
  _1_bit_adder u_1_bit_adder_11 (
    .A(_16_bit_A[10]), .B(_16_bit_B[10]), .Carry(n1_bit_adder_10_carry_out), .Sum(_32_bit_output[10]),
    .Carry_Out(n1_bit_adder_11_carry_out));
  _1_bit_adder u_1_bit_adder_12 (
    .A(_16_bit_A[11]), .B(_16_bit_B[11]), .Carry(n1_bit_adder_11_carry_out), .Sum(_32_bit_output[11]),
    .Carry_Out(n1_bit_adder_12_carry_out));
  _1_bit_adder u_1_bit_adder_13 (
    .A(_16_bit_A[12]), .B(_16_bit_B[12]), .Carry(n1_bit_adder_12_carry_out), .Sum(_32_bit_output[12]),
    .Carry_Out(n1_bit_adder_13_carry_out));
  _1_bit_adder u_1_bit_adder_14 (
    .A(_16_bit_A[13]), .B(_16_bit_B[13]), .Carry(n1_bit_adder_13_carry_out), .Sum(_32_bit_output[13]),
    .Carry_Out(n1_bit_adder_14_carry_out));
  _1_bit_adder u_1_bit_adder_15 (
    .A(_16_bit_A[14]), .B(_16_bit_B[14]), .Carry(n1_bit_adder_14_carry_out), .Sum(_32_bit_output[14]),
    .Carry_Out(n1_bit_adder_15_carry_out));
  _1_bit_adder u_1_bit_adder_16 (
    .A(_16_bit_A[15]), .B(_16_bit_B[15]), .Carry(n1_bit_adder_15_carry_out), .Sum(_32_bit_output[15]),
    .Carry_Out(Carryout));
endmodule

// fact
module myInst (
  input  [3:0] _3_bit_A,
  input  clk,
  output [31:0] _32_bit_C
);

  wire and_1_out, multiplexer_1_out, not_1_out, not_2_out, or_1_out, or_2_out, or_3_out;
  wire [3:0] counter_1_q, n4_bit_sub_1__4_bit_c;
  wire [15:0] bit_extender_1_out, bit_extender_2_out, multiplexer_2_out, multiplexer_3_out, multiplier_1_out,
       register_1_q;

  Multiplexer #(.enable("false")) multiplexer_1 (.in0(1'b0), .in1(1'b1), .out(multiplexer_1_out), .sel(or_1_out));
  _4_bit_sub u_4_bit_sub_1 (._4_bit_A(_3_bit_A), ._4_bit_B(4'b0001), ._4_bit_C(n4_bit_sub_1__4_bit_c));
  assign bit_extender_1_out = {{12{1'b0}}, _3_bit_A};  // Bit_Extender bit_extender_1
  Counter #(.width(4), .max('hf)) counter_1 (
    .load(1'b1), .D(n4_bit_sub_1__4_bit_c), .count(multiplexer_1_out), .Q(counter_1_q), .clk(clk));  // open: carry, clr
  Multiplexer #(.width(16), .enable("false")) multiplexer_2 (
    .in0(bit_extender_1_out), .in1(multiplier_1_out), .out(multiplexer_2_out), .sel(or_1_out));
  or or_1 (or_1_out, counter_1_q[3], counter_1_q[2], counter_1_q[1], counter_1_q[0]);
  assign bit_extender_2_out = {{12{counter_1_q[3]}}, counter_1_q};  // Bit_Extender bit_extender_2
  Register #(.width(16)) register_1 (.D(multiplexer_2_out), .Q(register_1_q), .clk(clk));  // open: en, clr
  Multiplier #(.width(16)) multiplier_1 (
    .a(register_1_q), .b(bit_extender_2_out), .out(multiplier_1_out));  // open: cin, cout
  and and_1 (and_1_out, or_2_out, or_3_out);
  or or_2 (or_2_out, counter_1_q[2], counter_1_q[3], counter_1_q[1], not_1_out);
  not not_1 (not_1_out, counter_1_q[0]);
  assign _32_bit_C = {{16{1'b0}}, multiplexer_3_out};  // Bit_Extender bit_extender_3
  Multiplexer #(.width(16), .enable("false")) multiplexer_3 (
    .in0(register_1_q), .in1({16{1'b0}}), .out(multiplexer_3_out), .sel(and_1_out));
  or or_3 (or_3_out, _3_bit_A[2], _3_bit_A[3], _3_bit_A[1], not_2_out);
  not not_2 (not_2_out, _3_bit_A[0]);
endmodule

// sub4
module _4_bit_sub (
  input  [3:0] _4_bit_A,
  input  [3:0] _4_bit_B,
  output [3:0] _4_bit_C
);

  wire n1_bit_adder_1_carry_out, n1_bit_adder_2_carry_out, n1_bit_adder_3_carry_out;
  wire [3:0] not_1_out;

  assign not_1_out = ~_4_bit_B;  // NOT_Gate not_1, 4 bits wide
  _1_bit_adder u_1_bit_adder_1 (
    .A(_4_bit_A[0]), .B(not_1_out[0]), .Carry(1'b1), .Sum(_4_bit_C[0]), .Carry_Out(n1_bit_adder_1_carry_out));
  _1_bit_adder u_1_bit_adder_2 (
    .A(_4_bit_A[1]), .B(not_1_out[1]), .Carry(n1_bit_adder_1_carry_out), .Sum(_4_bit_C[1]),
    .Carry_Out(n1_bit_adder_2_carry_out));
  _1_bit_adder u_1_bit_adder_3 (
    .A(_4_bit_A[2]), .B(not_1_out[2]), .Carry(n1_bit_adder_2_carry_out), .Sum(_4_bit_C[2]),
    .Carry_Out(n1_bit_adder_3_carry_out));
  _1_bit_adder u_1_bit_adder_4 (
    .A(_4_bit_A[3]), .B(not_1_out[3]), .Carry(n1_bit_adder_3_carry_out), .Sum(_4_bit_C[3]));  // open: Carry_Out
endmodule
