// Logisim project CPU.circ as structural Verilog: 1 circuit, main circuit main
// CPU
module main (
  input  in_1,
  output [31:0] Instruction
);

  wire alusrc, branch, CLK, memread, memtoreg, memwrite, multiplexer_1_out, not_1_out, not_2_out, regwrt,
       zero;
  wire [4:0] regdst;
  wire [7:0] counter_1_q, multiplexer_4_out, multiplexer_7_out, n8_bit_adder_1__8_bit_output, nextpc;
  wire [31:0] main_1__32_bit_c, multiplexer_10_out, ram_1_data, registerfile_1_p1, registerfile_1_p8,
       registerfile_1_p9;

  Multiplexer #(.select(4), .enable("false")) multiplexer_1 (
    .in0(1'b0), .in1(1'b0), .in2(1'b0), .in3(1'b0), .in4(1'b0), .in5(1'b0), .in6(1'b0), .in7(1'b0),
    .in8(1'b0), .in9(1'b0), .in10(1'b0), .in11(1'b0), .in12(zero), .in13(not_2_out), .in14(1'b1),
    .in15(zero), .out(multiplexer_1_out), .sel(Instruction[29:26]));
  not not_1 (not_1_out, multiplexer_1_out);
  Counter counter_1 (
    .load(multiplexer_1_out), .D(nextpc), .count(not_1_out), .Q(counter_1_q), .clk(CLK), .clr(in_1));  // open: carry
  not not_2 (not_2_out, zero);
  Multiplexer #(.select(4), .width(5), .enable("false")) multiplexer_2 (
    .in0(Instruction[15:11]), .in1(Instruction[15:11]), .in2(Instruction[15:11]), .in3(Instruction[15:11]),
    .in4(Instruction[15:11]), .in5(Instruction[15:11]), .in6(Instruction[15:11]), .in7(Instruction[15:11]),
    .in8(Instruction[15:11]), .in9(Instruction[15:11]), .in10(Instruction[20:16]), .in11(Instruction[15:11]),
    .in12(Instruction[15:11]), .in13(Instruction[15:11]), .in14(Instruction[15:11]),
    .in15(Instruction[20:16]), .out(regdst), .sel(Instruction[29:26]));
  Multiplexer #(.select(4), .enable("false")) multiplexer_3 (
    .in0(1'b0), .in1(1'b0), .in2(1'b0), .in3(1'b0), .in4(1'b0), .in5(1'b0), .in6(1'b0), .in7(1'b0),
    .in8(1'b0), .in9(1'b0), .in10(1'b1), .in11(1'b1), .in12(1'b0), .in13(1'b0), .in14(1'b0), .in15(1'b1),
    .out(alusrc), .sel(Instruction[29:26]));
  Clock clock_1 (.out(CLK));
  _8_bit_adder u_8_bit_adder_1 (
    ._8_bit_A(counter_1_q), ._8_bit_B(Instruction[7:0]), ._8_bit_Output(n8_bit_adder_1__8_bit_output));  // open: Cout
  Multiplexer #(.width(8), .enable("false")) multiplexer_4 (
    .in0(n8_bit_adder_1__8_bit_output), .in1(counter_1_q), .out(multiplexer_4_out), .sel(zero));
  ROM #(.dataWidth(32)) rom_1 (.addr(counter_1_q), .data(Instruction));  // open: sel
  Multiplexer #(.select(4), .enable("false")) multiplexer_5 (
    .in0(1'b0), .in1(1'b0), .in2(1'b0), .in3(1'b0), .in4(1'b0), .in5(1'b0), .in6(1'b0), .in7(1'b0),
    .in8(1'b0), .in9(1'b0), .in10(1'b0), .in11(1'b0), .in12(1'b1), .in13(1'b1), .in14(1'b0), .in15(1'b0),
    .out(branch), .sel(Instruction[29:26]));
  Multiplexer #(.select(4), .enable("false")) multiplexer_6 (
    .in0(1'b0), .in1(1'b0), .in2(1'b0), .in3(1'b0), .in4(1'b0), .in5(1'b0), .in6(1'b0), .in7(1'b0),
    .in8(1'b0), .in9(1'b0), .in10(1'b1), .in11(1'b0), .in12(1'b0), .in13(1'b0), .in14(1'b0), .in15(1'b0),
    .out(memtoreg), .sel(Instruction[29:26]));
  Multiplexer #(.width(8), .enable("false")) multiplexer_7 (
    .in0(counter_1_q), .in1(n8_bit_adder_1__8_bit_output), .out(multiplexer_7_out), .sel(zero));
  Multiplexer #(.select(4), .width(8), .disabled(0), .enable("false")) multiplexer_8 (
    .in0(counter_1_q), .in1(counter_1_q), .in2(counter_1_q), .in3(counter_1_q), .in4(counter_1_q),
    .in5(counter_1_q), .in6(counter_1_q), .in7(counter_1_q), .in8(counter_1_q), .in9(counter_1_q),
    .in10(counter_1_q), .in11(counter_1_q), .in12(multiplexer_7_out), .in13(multiplexer_4_out),
    .in14(Instruction[7:0]), .in15(counter_1_q), .out(nextpc), .sel(Instruction[29:26]));
  Multiplexer #(.select(4), .enable("false")) multiplexer_9 (
    .in0(1'b1), .in1(1'b1), .in2(1'b1), .in3(1'b1), .in4(1'b1), .in5(1'b1), .in6(1'b1), .in7(1'b1),
    .in8(1'b1), .in9(1'b1), .in10(1'b1), .in11(1'b0), .in12(1'b0), .in13(1'b0), .in14(1'b0), .in15(1'b1),
    .out(regwrt), .sel(Instruction[29:26]));
  // RegisterFile registerfile_1: pin names not known; wires that end beside it: registerfile_1_p1, CLK, regwrt, regdst, Instruction[25:21], Instruction[20:16], {16{1'b0}}, registerfile_1_p8, registerfile_1_p9
  Multiplexer #(.width(32), .enable("false")) multiplexer_10 (
    .in0(registerfile_1_p9), .in1({{16{1'b0}}, Instruction[15:0]}), .out(multiplexer_10_out), .sel(alusrc));
  Multiplexer #(.select(4), .enable("false")) multiplexer_11 (
    .in0(1'b0), .in1(1'b0), .in2(1'b0), .in3(1'b0), .in4(1'b0), .in5(1'b0), .in6(1'b0), .in7(1'b0),
    .in8(1'b0), .in9(1'b0), .in10(1'b1), .in11(1'b0), .in12(1'b0), .in13(1'b0), .in14(1'b0), .in15(1'b0),
    .out(memread), .sel(Instruction[29:26]));
  Multiplexer #(.select(4), .enable("false")) multiplexer_12 (
    .in0(1'b0), .in1(1'b0), .in2(1'b0), .in3(1'b0), .in4(1'b0), .in5(1'b0), .in6(1'b0), .in7(1'b0),
    .in8(1'b0), .in9(1'b0), .in10(1'b0), .in11(1'b1), .in12(1'b0), .in13(1'b0), .in14(1'b0), .in15(1'b0),
    .out(memwrite), .sel(Instruction[29:26]));
  ALU_main main_1 (
    ._32_bit_A(registerfile_1_p8), ._32_bit_B(multiplexer_10_out), .OpCode(Instruction[31:26]), .clk(CLK),
    ._32_bit_C(main_1__32_bit_c), .Zero(zero));  // open: Carryout, Overflow
  RAM #(.dataWidth(32), .bus("separate")) ram_1 (
    .addr(main_1__32_bit_c[7:0]), .din(registerfile_1_p9), .data(ram_1_data), .str(memwrite), .clk(CLK),
    .ld(memread));  // open: sel, clr
  Multiplexer #(.width(32), .enable("false")) multiplexer_13 (
    .in0(main_1__32_bit_c), .in1(ram_1_data), .out(registerfile_1_p1), .sel(memtoreg));

  // Other names for the same wires on the sheet: func[5:0] = Instruction[5:0]; immediate[15:0] = Instruction[15:0];
  //   JumpTarget[25:0] = Instruction[25:0]; shamt[4:0] = Instruction[10:6]; rd[4:0] = Instruction[15:11];
  //   rt[4:0] = Instruction[20:16]; rs[4:0] = Instruction[25:21]; opcode[5:0] = Instruction[31:26]; RST = in_1

  // Notes on the sheet:
  //   contents of rom_1 (hex, n*v repeats v):
  //   4001800 2968000a 296c0008 29690000 296a0001 92a5000 46a1800 1d036800 58b5800 31a0fffa 3800000b
endmodule
