// Logisim project mult.circ as structural Verilog: 4 circuits, main circuit main
module main (
  input  [15:0] _16_bit_A,
  input  [15:0] _16_bit_B,
  output [31:0] _32_bit_C
);

  wire [15:0] n16_bit_mult_with_1_bit_2__16_bit_output, n16_bit_mult_with_1_bit_3__16_bit_output,
       n16_bit_mult_with_1_bit_4__16_bit_output, n16_bit_mult_with_1_bit_5__16_bit_output,
       n16_bit_mult_with_1_bit_6__16_bit_output, n16_bit_mult_with_1_bit_7__16_bit_output,
       n16_bit_mult_with_1_bit_8__16_bit_output, n16_bit_mult_with_1_bit_9__16_bit_output,
       n16_bit_mult_with_1_bit_10__16_bit_output, n16_bit_mult_with_1_bit_11__16_bit_output,
       n16_bit_mult_with_1_bit_12__16_bit_output, n16_bit_mult_with_1_bit_13__16_bit_output,
       n16_bit_mult_with_1_bit_14__16_bit_output, n16_bit_mult_with_1_bit_15__16_bit_output,
       n16_bit_mult_with_1_bit_16__16_bit_output;
  wire [15:1] n16_bit_adder_1__32_bit_output, n16_bit_adder_2__32_bit_output, n16_bit_adder_3__32_bit_output,
       n16_bit_adder_4__32_bit_output, n16_bit_adder_5__32_bit_output, n16_bit_adder_6__32_bit_output,
       n16_bit_adder_7__32_bit_output, n16_bit_adder_8__32_bit_output, n16_bit_adder_9__32_bit_output,
       n16_bit_adder_10__32_bit_output, n16_bit_adder_11__32_bit_output, n16_bit_adder_12__32_bit_output,
       n16_bit_adder_13__32_bit_output, n16_bit_adder_14__32_bit_output,
       n16_bit_mult_with_1_bit_1__16_bit_output;
  wire [15:15] n16_bit_adder_1_carryout, n16_bit_adder_2_carryout, n16_bit_adder_3_carryout,
       n16_bit_adder_4_carryout, n16_bit_adder_5_carryout, n16_bit_adder_6_carryout,
       n16_bit_adder_7_carryout, n16_bit_adder_8_carryout, n16_bit_adder_9_carryout,
       n16_bit_adder_10_carryout, n16_bit_adder_11_carryout, n16_bit_adder_12_carryout,
       n16_bit_adder_13_carryout, n16_bit_adder_14_carryout;

  _16_bit_mult_with_1_bit u_16_bit_mult_with_1_bit_1 (
    ._16_bit_A(_16_bit_A), ._1_bit_of_B(_16_bit_B[0]),
    ._16_bit_output({n16_bit_mult_with_1_bit_1__16_bit_output, _32_bit_C[0]}));
  _16_bit_mult_with_1_bit u_16_bit_mult_with_1_bit_2 (
    ._16_bit_A(_16_bit_A), ._1_bit_of_B(_16_bit_B[1]),
    ._16_bit_output(n16_bit_mult_with_1_bit_2__16_bit_output));
  _16_bit_mult_with_1_bit u_16_bit_mult_with_1_bit_3 (
    ._16_bit_A(_16_bit_A), ._1_bit_of_B(_16_bit_B[2]),
    ._16_bit_output(n16_bit_mult_with_1_bit_3__16_bit_output));
  _16_bit_mult_with_1_bit u_16_bit_mult_with_1_bit_4 (
    ._16_bit_A(_16_bit_A), ._1_bit_of_B(_16_bit_B[3]),
    ._16_bit_output(n16_bit_mult_with_1_bit_4__16_bit_output));
  _16_bit_mult_with_1_bit u_16_bit_mult_with_1_bit_5 (
    ._16_bit_A(_16_bit_A), ._1_bit_of_B(_16_bit_B[4]),
    ._16_bit_output(n16_bit_mult_with_1_bit_5__16_bit_output));
  _16_bit_mult_with_1_bit u_16_bit_mult_with_1_bit_6 (
    ._16_bit_A(_16_bit_A), ._1_bit_of_B(_16_bit_B[5]),
    ._16_bit_output(n16_bit_mult_with_1_bit_6__16_bit_output));
  _16_bit_mult_with_1_bit u_16_bit_mult_with_1_bit_7 (
    ._16_bit_A(_16_bit_A), ._1_bit_of_B(_16_bit_B[6]),
    ._16_bit_output(n16_bit_mult_with_1_bit_7__16_bit_output));
  _16_bit_mult_with_1_bit u_16_bit_mult_with_1_bit_8 (
    ._16_bit_A(_16_bit_A), ._1_bit_of_B(_16_bit_B[7]),
    ._16_bit_output(n16_bit_mult_with_1_bit_8__16_bit_output));
  _16_bit_mult_with_1_bit u_16_bit_mult_with_1_bit_9 (
    ._16_bit_A(_16_bit_A), ._1_bit_of_B(_16_bit_B[8]),
    ._16_bit_output(n16_bit_mult_with_1_bit_9__16_bit_output));
  _16_bit_mult_with_1_bit u_16_bit_mult_with_1_bit_10 (
    ._16_bit_A(_16_bit_A), ._1_bit_of_B(_16_bit_B[9]),
    ._16_bit_output(n16_bit_mult_with_1_bit_10__16_bit_output));
  _16_bit_mult_with_1_bit u_16_bit_mult_with_1_bit_11 (
    ._16_bit_A(_16_bit_A), ._1_bit_of_B(_16_bit_B[10]),
    ._16_bit_output(n16_bit_mult_with_1_bit_11__16_bit_output));
  _16_bit_mult_with_1_bit u_16_bit_mult_with_1_bit_12 (
    ._16_bit_A(_16_bit_A), ._1_bit_of_B(_16_bit_B[11]),
    ._16_bit_output(n16_bit_mult_with_1_bit_12__16_bit_output));
  _16_bit_mult_with_1_bit u_16_bit_mult_with_1_bit_13 (
    ._16_bit_A(_16_bit_A), ._1_bit_of_B(_16_bit_B[12]),
    ._16_bit_output(n16_bit_mult_with_1_bit_13__16_bit_output));
  _16_bit_mult_with_1_bit u_16_bit_mult_with_1_bit_14 (
    ._16_bit_A(_16_bit_A), ._1_bit_of_B(_16_bit_B[13]),
    ._16_bit_output(n16_bit_mult_with_1_bit_14__16_bit_output));
  _16_bit_mult_with_1_bit u_16_bit_mult_with_1_bit_15 (
    ._16_bit_A(_16_bit_A), ._1_bit_of_B(_16_bit_B[14]),
    ._16_bit_output(n16_bit_mult_with_1_bit_15__16_bit_output));
  _16_bit_mult_with_1_bit u_16_bit_mult_with_1_bit_16 (
    ._16_bit_A(_16_bit_A), ._1_bit_of_B(_16_bit_B[15]),
    ._16_bit_output(n16_bit_mult_with_1_bit_16__16_bit_output));
  _16_bit_adder u_16_bit_adder_1 (
    ._16_bit_A({1'b0, n16_bit_mult_with_1_bit_1__16_bit_output}),
    ._16_bit_B(n16_bit_mult_with_1_bit_2__16_bit_output),
    ._32_bit_output({n16_bit_adder_1__32_bit_output, _32_bit_C[1]}), .Carryout(n16_bit_adder_1_carryout[15]));
  _16_bit_adder u_16_bit_adder_2 (
    ._16_bit_A({n16_bit_adder_1_carryout[15], n16_bit_adder_1__32_bit_output}),
    ._16_bit_B(n16_bit_mult_with_1_bit_3__16_bit_output),
    ._32_bit_output({n16_bit_adder_2__32_bit_output, _32_bit_C[2]}), .Carryout(n16_bit_adder_2_carryout[15]));
  _16_bit_adder u_16_bit_adder_3 (
    ._16_bit_A({n16_bit_adder_2_carryout[15], n16_bit_adder_2__32_bit_output}),
    ._16_bit_B(n16_bit_mult_with_1_bit_4__16_bit_output),
    ._32_bit_output({n16_bit_adder_3__32_bit_output, _32_bit_C[3]}), .Carryout(n16_bit_adder_3_carryout[15]));
  _16_bit_adder u_16_bit_adder_4 (
    ._16_bit_A({n16_bit_adder_3_carryout[15], n16_bit_adder_3__32_bit_output}),
    ._16_bit_B(n16_bit_mult_with_1_bit_5__16_bit_output),
    ._32_bit_output({n16_bit_adder_4__32_bit_output, _32_bit_C[4]}), .Carryout(n16_bit_adder_4_carryout[15]));
  _16_bit_adder u_16_bit_adder_5 (
    ._16_bit_A({n16_bit_adder_4_carryout[15], n16_bit_adder_4__32_bit_output}),
    ._16_bit_B(n16_bit_mult_with_1_bit_6__16_bit_output),
    ._32_bit_output({n16_bit_adder_5__32_bit_output, _32_bit_C[5]}), .Carryout(n16_bit_adder_5_carryout[15]));
  _16_bit_adder u_16_bit_adder_6 (
    ._16_bit_A({n16_bit_adder_5_carryout[15], n16_bit_adder_5__32_bit_output}),
    ._16_bit_B(n16_bit_mult_with_1_bit_7__16_bit_output),
    ._32_bit_output({n16_bit_adder_6__32_bit_output, _32_bit_C[6]}), .Carryout(n16_bit_adder_6_carryout[15]));
  _16_bit_adder u_16_bit_adder_7 (
    ._16_bit_A({n16_bit_adder_6_carryout[15], n16_bit_adder_6__32_bit_output}),
    ._16_bit_B(n16_bit_mult_with_1_bit_8__16_bit_output),
    ._32_bit_output({n16_bit_adder_7__32_bit_output, _32_bit_C[7]}), .Carryout(n16_bit_adder_7_carryout[15]));
  _16_bit_adder u_16_bit_adder_8 (
    ._16_bit_A({n16_bit_adder_7_carryout[15], n16_bit_adder_7__32_bit_output}),
    ._16_bit_B(n16_bit_mult_with_1_bit_9__16_bit_output),
    ._32_bit_output({n16_bit_adder_8__32_bit_output, _32_bit_C[8]}), .Carryout(n16_bit_adder_8_carryout[15]));
  _16_bit_adder u_16_bit_adder_9 (
    ._16_bit_A({n16_bit_adder_8_carryout[15], n16_bit_adder_8__32_bit_output}),
    ._16_bit_B(n16_bit_mult_with_1_bit_10__16_bit_output),
    ._32_bit_output({n16_bit_adder_9__32_bit_output, _32_bit_C[9]}), .Carryout(n16_bit_adder_9_carryout[15]));
  _16_bit_adder u_16_bit_adder_10 (
    ._16_bit_A({n16_bit_adder_9_carryout[15], n16_bit_adder_9__32_bit_output}),
    ._16_bit_B(n16_bit_mult_with_1_bit_11__16_bit_output),
    ._32_bit_output({n16_bit_adder_10__32_bit_output, _32_bit_C[10]}),
    .Carryout(n16_bit_adder_10_carryout[15]));
  _16_bit_adder u_16_bit_adder_11 (
    ._16_bit_A({n16_bit_adder_10_carryout[15], n16_bit_adder_10__32_bit_output}),
    ._16_bit_B(n16_bit_mult_with_1_bit_12__16_bit_output),
    ._32_bit_output({n16_bit_adder_11__32_bit_output, _32_bit_C[11]}),
    .Carryout(n16_bit_adder_11_carryout[15]));
  _16_bit_adder u_16_bit_adder_12 (
    ._16_bit_A({n16_bit_adder_11_carryout[15], n16_bit_adder_11__32_bit_output}),
    ._16_bit_B(n16_bit_mult_with_1_bit_13__16_bit_output),
    ._32_bit_output({n16_bit_adder_12__32_bit_output, _32_bit_C[12]}),
    .Carryout(n16_bit_adder_12_carryout[15]));
  _16_bit_adder u_16_bit_adder_13 (
    ._16_bit_A({n16_bit_adder_12_carryout[15], n16_bit_adder_12__32_bit_output}),
    ._16_bit_B(n16_bit_mult_with_1_bit_14__16_bit_output),
    ._32_bit_output({n16_bit_adder_13__32_bit_output, _32_bit_C[13]}),
    .Carryout(n16_bit_adder_13_carryout[15]));
  _16_bit_adder u_16_bit_adder_14 (
    ._16_bit_A({n16_bit_adder_13_carryout[15], n16_bit_adder_13__32_bit_output}),
    ._16_bit_B(n16_bit_mult_with_1_bit_15__16_bit_output),
    ._32_bit_output({n16_bit_adder_14__32_bit_output, _32_bit_C[14]}),
    .Carryout(n16_bit_adder_14_carryout[15]));
  _16_bit_adder u_16_bit_adder_15 (
    ._16_bit_A({n16_bit_adder_14_carryout[15], n16_bit_adder_14__32_bit_output}),
    ._16_bit_B(n16_bit_mult_with_1_bit_16__16_bit_output), ._32_bit_output(_32_bit_C[30:15]),
    .Carryout(_32_bit_C[31]));
endmodule

module _16_bit_mult_with_1_bit (
  input  [15:0] _16_bit_A,
  input  _1_bit_of_B,
  output [15:0] _16_bit_output
);

  assign _16_bit_output = _16_bit_A & {16{_1_bit_of_B}};  // AND_Gate and_1, 16 bits wide
endmodule

module _16_bit_adder (
  input  [15:0] _16_bit_A,
  input  [15:0] _16_bit_B,
  output [15:0] _32_bit_output,
  output Carryout
);

  wire n1_bit_adder_1_carry_out, n1_bit_adder_2_carry_out, n1_bit_adder_3_carry_out,
       n1_bit_adder_4_carry_out, n1_bit_adder_5_carry_out, n1_bit_adder_6_carry_out,
       n1_bit_adder_7_carry_out, n1_bit_adder_8_carry_out, n1_bit_adder_9_carry_out,
       n1_bit_adder_10_carry_out, n1_bit_adder_11_carry_out, n1_bit_adder_12_carry_out,
       n1_bit_adder_13_carry_out, n1_bit_adder_14_carry_out, n1_bit_adder_15_carry_out;

  _1_bit_adder u_1_bit_adder_1 (
    .A(_16_bit_A[0]), .B(_16_bit_B[0]), .Carry(1'b0), .Sum(_32_bit_output[0]),
    .Carry_Out(n1_bit_adder_1_carry_out));
  _1_bit_adder u_1_bit_adder_2 (
    .A(_16_bit_A[1]), .B(_16_bit_B[1]), .Carry(n1_bit_adder_1_carry_out), .Sum(_32_bit_output[1]),
    .Carry_Out(n1_bit_adder_2_carry_out));
  _1_bit_adder u_1_bit_adder_3 (
    .A(_16_bit_A[2]), .B(_16_bit_B[2]), .Carry(n1_bit_adder_2_carry_out), .Sum(_32_bit_output[2]),
    .Carry_Out(n1_bit_adder_3_carry_out));
  _1_bit_adder u_1_bit_adder_4 (
    .A(_16_bit_A[3]), .B(_16_bit_B[3]), .Carry(n1_bit_adder_3_carry_out), .Sum(_32_bit_output[3]),
    .Carry_Out(n1_bit_adder_4_carry_out));
  _1_bit_adder u_1_bit_adder_5 (
    .A(_16_bit_A[4]), .B(_16_bit_B[4]), .Carry(n1_bit_adder_4_carry_out), .Sum(_32_bit_output[4]),
    .Carry_Out(n1_bit_adder_5_carry_out));
  _1_bit_adder u_1_bit_adder_6 (
    .A(_16_bit_A[5]), .B(_16_bit_B[5]), .Carry(n1_bit_adder_5_carry_out), .Sum(_32_bit_output[5]),
    .Carry_Out(n1_bit_adder_6_carry_out));
  _1_bit_adder u_1_bit_adder_7 (
    .A(_16_bit_A[6]), .B(_16_bit_B[6]), .Carry(n1_bit_adder_6_carry_out), .Sum(_32_bit_output[6]),
    .Carry_Out(n1_bit_adder_7_carry_out));
  _1_bit_adder u_1_bit_adder_8 (
    .A(_16_bit_A[7]), .B(_16_bit_B[7]), .Carry(n1_bit_adder_7_carry_out), .Sum(_32_bit_output[7]),
    .Carry_Out(n1_bit_adder_8_carry_out));
  _1_bit_adder u_1_bit_adder_9 (
    .A(_16_bit_A[8]), .B(_16_bit_B[8]), .Carry(n1_bit_adder_8_carry_out), .Sum(_32_bit_output[8]),
    .Carry_Out(n1_bit_adder_9_carry_out));
  _1_bit_adder u_1_bit_adder_10 (
    .A(_16_bit_A[9]), .B(_16_bit_B[9]), .Carry(n1_bit_adder_9_carry_out), .Sum(_32_bit_output[9]),
    .Carry_Out(n1_bit_adder_10_carry_out));
  _1_bit_adder u_1_bit_adder_11 (
    .A(_16_bit_A[10]), .B(_16_bit_B[10]), .Carry(n1_bit_adder_10_carry_out), .Sum(_32_bit_output[10]),
    .Carry_Out(n1_bit_adder_11_carry_out));
  _1_bit_adder u_1_bit_adder_12 (
    .A(_16_bit_A[11]), .B(_16_bit_B[11]), .Carry(n1_bit_adder_11_carry_out), .Sum(_32_bit_output[11]),
    .Carry_Out(n1_bit_adder_12_carry_out));
  _1_bit_adder u_1_bit_adder_13 (
    .A(_16_bit_A[12]), .B(_16_bit_B[12]), .Carry(n1_bit_adder_12_carry_out), .Sum(_32_bit_output[12]),
    .Carry_Out(n1_bit_adder_13_carry_out));
  _1_bit_adder u_1_bit_adder_14 (
    .A(_16_bit_A[13]), .B(_16_bit_B[13]), .Carry(n1_bit_adder_13_carry_out), .Sum(_32_bit_output[13]),
    .Carry_Out(n1_bit_adder_14_carry_out));
  _1_bit_adder u_1_bit_adder_15 (
    .A(_16_bit_A[14]), .B(_16_bit_B[14]), .Carry(n1_bit_adder_14_carry_out), .Sum(_32_bit_output[14]),
    .Carry_Out(n1_bit_adder_15_carry_out));
  _1_bit_adder u_1_bit_adder_16 (
    .A(_16_bit_A[15]), .B(_16_bit_B[15]), .Carry(n1_bit_adder_15_carry_out), .Sum(_32_bit_output[15]),
    .Carry_Out(Carryout));
endmodule

module _1_bit_adder (
  input  A,
  input  B,
  input  Carry,
  output Sum,
  output Carry_Out
);

  wire and_1_out, and_2_out, xor_1_out;

  xor xor_1 (xor_1_out, A, B);
  xor xor_2 (Sum, xor_1_out, Carry);
  and and_1 (and_1_out, Carry, xor_1_out);
  and and_2 (and_2_out, A, B);
  or or_1 (Carry_Out, and_1_out, and_2_out);

  // Other names for the same wires on the sheet: C = Carry
endmodule
